# Fritzing sketch wiringDiagram (saved by Fritzing 0.9.3b)

parts:
  Part1 = Arduino Uno (Rev3)
  Part2 = Soil Moisture Sensor
  VCC1 = Battery block 9V  # not connected
  7_Segment2 = 7 Segment Display
  R1 = Resistor [tolerance=±5% resistance=1k package="2010 [SMD]"]

nets:
  N1: Part1.A0, Part2.SIG
  N2: Part1.D8, 7_Segment2.Segment_G
  N3: Part1.D9_PWM, 7_Segment2.Segment_DP
  GND: Part1.GND, Part2.GND, R1.Pin_1
  N4: Part1.D2, 7_Segment2.Segment_A
  N5: Part1.D3_PWM, 7_Segment2.Segment_B
  N6: Part1.D4, 7_Segment2.Segment_C
  N7: Part1.D5_PWM, 7_Segment2.Segment_D
  N8: Part1.D6_PWM, 7_Segment2.Segment_E
  N9: Part1.D7, 7_Segment2.Segment_F
  5V: Part1.5V, Part2.VCC
  N10: 7_Segment2.common_anode, R1.Pin_0
